// Logisim project beag_harvard_rom.circ as structural Verilog: 1 circuit, main circuit main
module main (
);

  wire and_3_out, and_4_out, and_5_out, and_7_out, and_8_out, and_9_out, and_10_out, and_11_out, Bltz, Bnz,
       Bz, clock_1_out, clock_2_out, clock_3_out, clock_4_out, clock_5_out, clock_6_out, clock_7_out,
       clock_8_out, clock_9_out, clock_10_out, clock_11_out, comparator_2_eq, comparator_3_eq,
       comparator_4_eq, comparator_5_eq, decoder_1_out1, decoder_1_out2, decoder_1_out3, decoder_1_out4,
       decoder_1_out5, decoder_1_out6, decoder_1_out7, I_R, ImmExt, Jalr, Keyboard_1_avail, MemR, MemW, RegW,
       XeqY, XltY;
  wire [0:0] PCsel;
  wire [1:0] or_2_out, priority_encoder_1_out, SrcSel;
  wire [1:1] priority_encoder_1_gs;
  wire [2:0] ArithCode, Dsel, Xsel, Ysel;
  wire [2:2] not_1_out;
  wire [3:0] multiplexer_4_out_2;
  wire [6:0] Keyboard_1_data, multiplexer_5_out;
  wire [7:0] Imm, multiplexer_7_out_2;
  wire [11:0] multiplexer_4_out;
  wire [15:0] adder_1_out, adder_2_out, adder_3_out, and_2_out, bit_extender_1_out, bit_extender_2_out,
       bit_extender_3_out, bit_extender_4_out, Data_RAM_dout, divider_1_out, divider_1_rem,
       multiplexer_1_out, multiplexer_2_out, multiplexer_3_out, multiplexer_8_out, multiplier_1_out, PC_q,
       register_1_q, register_2_q, register_3_q, register_4_q, register_5_q, register_6_q, register_7_q,
       subtractor_1_out, xor_1_out;
  wire [15:7] multiplexer_5_out_2;
  wire [15:8] multiplexer_7_out, Program_ROM_data;

  assign bit_extender_1_out = {{8{Imm[7]}}, Imm};  // Bit_Extender bit_extender_1
  Multiplexer #(.width(16)) multiplexer_1 (
    .in0({Imm, multiplexer_7_out_2}), .in1(bit_extender_1_out), .out(multiplexer_1_out), .sel(ImmExt));
  Adder #(.width(16)) adder_1 (.a(PC_q), .b(16'h1), .out(adder_1_out));  // open: cin, cout
  Adder #(.width(16)) adder_2 (.a(PC_q), .b(bit_extender_1_out), .out(adder_2_out));  // open: cin, cout
  Register #(.width(16)) PC (.D(multiplexer_2_out), .en(1'b1), .clk(clock_1_out), .Q(PC_q));  // open: clr
  Multiplexer #(.select(2), .width(16)) multiplexer_2 (
    .in0(adder_1_out), .in1(adder_2_out), .in2({multiplexer_7_out, multiplexer_7_out_2}),
    .out(multiplexer_2_out), .sel({Jalr, PCsel[0]}));  // open: in3
  Clock clock_1 (.out(clock_1_out));
  Multiplexer #(.select(2), .width(16)) multiplexer_3 (
    .in0({multiplexer_7_out, multiplexer_7_out_2}), .in1(multiplexer_8_out), .in2(multiplexer_1_out),
    .in3(adder_1_out), .out(multiplexer_3_out), .sel(SrcSel));
  Decoder #(.enable("false"), .select(3)) decoder_1 (
    .out1(decoder_1_out1), .out2(decoder_1_out2), .out3(decoder_1_out3), .out4(decoder_1_out4),
    .out5(decoder_1_out5), .out6(decoder_1_out6), .out7(decoder_1_out7), .sel(Dsel));  // open: out0
  Register #(.width(16)) register_1 (
    .D(multiplexer_3_out), .en(decoder_1_out2), .clk(clock_2_out), .Q(register_1_q));  // open: clr
  Clock clock_2 (.out(clock_2_out));
  Register #(.width(16)) register_2 (
    .D(multiplexer_3_out), .en(decoder_1_out4), .clk(clock_3_out), .Q(register_2_q));  // open: clr
  Clock clock_3 (.out(clock_3_out));
  Register #(.width(16)) register_3 (
    .D(multiplexer_3_out), .en(decoder_1_out6), .clk(clock_4_out), .Q(register_3_q));  // open: clr
  Clock clock_4 (.out(clock_4_out));
  ROM #(.addrWidth(12), .dataWidth(16)) Program_ROM (.addr(PC_q[11:0]), .data({Program_ROM_data, Imm}));
  Register #(.width(16)) register_4 (
    .D(multiplexer_3_out), .en(decoder_1_out1), .clk(clock_5_out), .Q(register_4_q));  // open: clr
  Clock clock_5 (.out(clock_5_out));
  Register #(.width(16)) register_5 (
    .D(multiplexer_3_out), .en(decoder_1_out3), .clk(clock_6_out), .Q(register_5_q));  // open: clr
  Clock clock_6 (.out(clock_6_out));
  Register #(.width(16)) register_6 (
    .D(multiplexer_3_out), .en(decoder_1_out5), .clk(clock_7_out), .Q(register_6_q));  // open: clr
  Clock clock_7 (.out(clock_7_out));
  Register #(.width(16)) register_7 (
    .D(multiplexer_3_out), .en(decoder_1_out7), .clk(clock_8_out), .Q(register_7_q));  // open: clr
  Clock clock_8 (.out(clock_8_out));
  Multiplexer #(.select(3), .width(16)) multiplexer_4 (
    .in0({16{1'b0}}), .in1(register_4_q), .in2(register_1_q), .in3(register_5_q), .in4(register_2_q),
    .in5(register_6_q), .in6(register_3_q), .in7(register_7_q),
    .out({multiplexer_4_out_2, multiplexer_4_out}), .sel(Xsel));
  assign bit_extender_2_out = {{15{multiplexer_4_out_2[3]}}, multiplexer_4_out_2[3]};  // Bit_Extender bit_extender_2
  Multiplexer #(.select(3), .width(16)) multiplexer_5 (
    .in0({16{1'b0}}), .in1(register_4_q), .in2(register_1_q), .in3(register_5_q), .in4(register_2_q),
    .in5(register_6_q), .in6(register_3_q), .in7(register_7_q),
    .out({multiplexer_5_out_2, multiplexer_5_out}), .sel(Ysel));
  not not_1 (not_1_out[2], I_R);
  assign Ysel = Imm[2:0] & {3{not_1_out[2]}};  // AND_Gate and_1, 3 bits wide
  Multiplexer #(.width(3)) multiplexer_6 (.in0(Imm[6:4]), .in1(Program_ROM_data[10:8]), .out(Xsel), .sel(I_R));
  ROM #(.addrWidth(4), .dataWidth(14)) Control_ROM (
    .addr(Program_ROM_data[15:12]),
    .data({Bltz, Bz, Bnz, Jalr, MemW, MemR, ImmExt, SrcSel, RegW, I_R, ArithCode}));
  Adder #(.width(16)) adder_3 (
    .a({multiplexer_4_out_2, multiplexer_4_out}), .b({multiplexer_5_out_2, multiplexer_5_out}),
    .out(adder_3_out));  // open: cin, cout
  Subtractor #(.width(16)) subtractor_1 (
    .a({multiplexer_4_out_2, multiplexer_4_out}), .b({multiplexer_5_out_2, multiplexer_5_out}),
    .out(subtractor_1_out));  // open: bin, bout
  Multiplier #(.mode("twosComplement"), .width(16)) multiplier_1 (
    .a({multiplexer_4_out_2, multiplexer_4_out}), .b({multiplexer_5_out_2, multiplexer_5_out}),
    .out(multiplier_1_out));  // open: cin, cout
  Divider #(.mode("twosComplement"), .width(16)) divider_1 (
    .a({multiplexer_4_out_2, multiplexer_4_out}), .b({multiplexer_5_out_2, multiplexer_5_out}),
    .out(divider_1_out), .upper(bit_extender_2_out), .rem(divider_1_rem));
  Comparator #(.width(16)) comparator_1 (
    .a({multiplexer_4_out_2, multiplexer_4_out}), .b({multiplexer_5_out_2, multiplexer_5_out}), .eq(XeqY),
    .lt(XltY));  // open: gt
  assign and_2_out = {multiplexer_4_out_2, multiplexer_4_out} & ~{multiplexer_5_out_2, multiplexer_5_out};  // AND_Gate and_2, 16 bits wide
  assign xor_1_out = {multiplexer_4_out_2, multiplexer_4_out} ^ {multiplexer_5_out_2, multiplexer_5_out};  // XOR_Gate xor_1, 16 bits wide
  and and_3 (and_3_out, Bnz, ~XeqY);  // AND_Gate
  and and_4 (and_4_out, Bz, XeqY);
  and and_5 (and_5_out, Bltz, XltY);
  Multiplexer #(.select(3), .width(16)) multiplexer_7 (
    .in0(adder_3_out), .in1(subtractor_1_out), .in2(multiplier_1_out), .in3(divider_1_out), .in4(and_2_out),
    .in5(xor_1_out), .in7(divider_1_rem), .out({multiplexer_7_out, multiplexer_7_out_2}), .sel(ArithCode));  // open: in6
  or or_1 (PCsel[0], and_3_out, and_4_out, and_5_out);
  assign Dsel = Program_ROM_data[10:8] & {3{RegW}};  // AND_Gate and_6, 3 bits wide
  Comparator #(.width(4)) comparator_2 (.a(multiplexer_4_out_2), .b(4'b0010), .eq(comparator_2_eq));  // open: gt, lt
  Comparator #(.width(16)) comparator_3 (
    .a({multiplexer_4_out_2, multiplexer_4_out}), .b(16'h4000), .eq(comparator_3_eq));  // open: gt, lt
  Comparator #(.width(16)) comparator_4 (
    .a({multiplexer_4_out_2, multiplexer_4_out}), .b(16'h4002), .eq(comparator_4_eq));  // open: gt, lt
  Comparator #(.width(16)) comparator_5 (
    .a({multiplexer_4_out_2, multiplexer_4_out}), .b(16'h4001), .eq(comparator_5_eq));  // open: gt, lt
  and and_7 (and_7_out, comparator_2_eq, MemW);
  and and_8 (and_8_out, comparator_2_eq, MemR);
  and and_9 (and_9_out, comparator_3_eq, MemW);
  and and_10 (and_10_out, comparator_4_eq, MemR);
  and and_11 (and_11_out, comparator_5_eq, MemR);
  RAM #(.addrWidth(12), .dataWidth(16), .enables("line")) Data_RAM (
    .addr(multiplexer_4_out), .we(and_7_out), .clk(clock_9_out),
    .din({multiplexer_5_out_2, multiplexer_5_out}), .dout(Data_RAM_dout));
  Clock clock_9 (.out(clock_9_out));
  TTY TTY_1 (.data(multiplexer_5_out), .clk(clock_10_out), .we(and_9_out));  // open: clr
  Clock clock_10 (.out(clock_10_out));
  Clock clock_11 (.out(clock_11_out));
  Keyboard Keyboard_1 (
    .clk(clock_11_out), .re(and_10_out), .avail(Keyboard_1_avail), .data(Keyboard_1_data));  // open: clr
  assign bit_extender_3_out = {{9{1'b0}}, Keyboard_1_data};  // Bit_Extender bit_extender_3
  assign bit_extender_4_out = {{15{1'b0}}, Keyboard_1_avail};  // Bit_Extender bit_extender_4
  Multiplexer #(.select(2), .width(16)) multiplexer_8 (
    .in0(Data_RAM_dout), .in1(bit_extender_3_out), .in2(bit_extender_4_out), .in3({16{1'b0}}),
    .out(multiplexer_8_out), .sel(or_2_out));
  assign or_2_out = ~{2{priority_encoder_1_gs[1]}} | priority_encoder_1_out;  // OR_Gate or_2, 2 bits wide
  Priority_Encoder #(.select(2)) priority_encoder_1 (
    .in0(and_8_out), .in1(and_10_out), .in2(and_11_out), .out(priority_encoder_1_out),
    .gs(priority_encoder_1_gs[1]));  // open: in3, en_out, en_in

  // Other names for the same wires on the sheet: PCsel[1] = Jalr

  // Notes on the sheet:
  //   R2
  //   R4
  //   R6
  //   contents of Program_ROM (hex, n*v repeats v):
  //   9100 8140 9201 8240 9302 8340 9700 6420 e4ff 6430 950a 1645 e60b 9530 1645 f6f8 9531 1554 f5f5 9402
  //   2774 776 e0f1 940a 9530 9301 8300 9200 8220 5020 223 7674 665 5026 223 3774 d7fb 1223 6620 e603 5016
  //   e0fc e000
  //   R0
  //   R1
  //   R3
  //   R5
  //   R7
  //   Y
  //   X
  //   Dst
  //   Beag Computer (Harward Architecture)
  //   X
  //   X sign-extended
  //   Y
  //   contents of Control_ROM (hex, n*v repeats v):
  //   10 11 12 13 470 200 130 17 58 d8 14 15 0 808 1008 2008
  //   ALU
  //   Branch condition
  //   Data In
  //   Address
  //   Data Out
  //   Instruction decoder
  //   Display
  //   Keyboard
endmodule
