// Logisim project beag_von_neumann_rom.circ as structural Verilog: 1 circuit, main circuit main
module main (
);

  wire and_3_out, and_4_out, and_5_out, and_7_out, and_8_out, and_9_out, and_10_out, and_11_out, and_12_out,
       Bltz, Bnz, Bz, clock_1_out, clock_2_out, clock_3_out, clock_4_out, clock_5_out, clock_6_out,
       clock_7_out, clock_8_out, clock_9_out, clock_10_out, clock_11_out, clock_12_out, clock_13_out,
       comparator_2_eq, comparator_3_eq, comparator_4_eq, comparator_5_eq, comparator_6_eq, decoder_1_out1,
       decoder_1_out2, decoder_1_out3, decoder_1_out4, decoder_1_out5, decoder_1_out6, decoder_1_out7,
       execute, fetch, I_R, ImmExt, Jalr, Keyboard_1_avail, MemR, MemRx, MemW, RegW, XeqY, XltY;
  wire [0:0] PCsel;
  wire [1:0] SrcSel;
  wire [2:0] ArithCode, Dsel, or_3_out, priority_encoder_1_out, Xsel, Ysel;
  wire [2:2] not_1_out, priority_encoder_1_gs;
  wire [6:0] Keyboard_1_data, multiplexer_6_out;
  wire [7:0] Imm, multiplexer_8_out_2;
  wire [14:0] multiplexer_5_out;
  wire [15:0] adder_1_out, adder_2_out, adder_3_out, and_2_out, bit_extender_1_out, bit_extender_2_out,
       bit_extender_3_out, bit_extender_4_out, divider_1_out, divider_1_rem, IR_q, multiplexer_1_out,
       multiplexer_2_out, multiplexer_3_out, multiplexer_9_out, multiplexer_10_out, multiplier_1_out, PC,
       RAM_1_dout, register_1_q, register_2_q, register_3_q, register_4_q, register_5_q, register_6_q,
       register_7_q, ROM_1_data, subtractor_1_out, xor_1_out;
  wire [15:7] multiplexer_6_out_2;
  wire [15:8] multiplexer_4_out, multiplexer_8_out;
  wire [15:15] multiplexer_5_out_2;

  assign bit_extender_1_out = {{8{Imm[7]}}, Imm};  // Bit_Extender bit_extender_1
  Multiplexer #(.width(16)) multiplexer_1 (
    .in0({Imm, multiplexer_8_out_2}), .in1(bit_extender_1_out), .out(multiplexer_1_out), .sel(ImmExt));
  Adder #(.width(16)) adder_1 (.a(PC), .b(16'h1), .out(adder_1_out));  // open: cin, cout
  Adder #(.width(16)) adder_2 (.a(PC), .b(bit_extender_1_out), .out(adder_2_out));  // open: cin, cout
  Register #(.width(16)) u_PC (.D(multiplexer_2_out), .en(execute), .clk(clock_1_out), .Q(PC));  // open: clr
  Multiplexer #(.select(2), .width(16)) multiplexer_2 (
    .in0(adder_1_out), .in1(adder_2_out), .in2({multiplexer_8_out, multiplexer_8_out_2}),
    .out(multiplexer_2_out), .sel({Jalr, PCsel[0]}));  // open: in3
  Clock clock_1 (.out(clock_1_out));
  Multiplexer #(.select(2), .width(16)) multiplexer_3 (
    .in0({multiplexer_8_out, multiplexer_8_out_2}), .in1(multiplexer_10_out), .in2(multiplexer_1_out),
    .in3(adder_1_out), .out(multiplexer_3_out), .sel(SrcSel));
  Decoder #(.enable("false"), .select(3)) decoder_1 (
    .out1(decoder_1_out1), .out2(decoder_1_out2), .out3(decoder_1_out3), .out4(decoder_1_out4),
    .out5(decoder_1_out5), .out6(decoder_1_out6), .out7(decoder_1_out7), .sel(Dsel));  // open: out0
  Register #(.width(16)) register_1 (
    .D(multiplexer_3_out), .en(decoder_1_out2), .clk(clock_2_out), .Q(register_1_q));  // open: clr
  Clock clock_2 (.out(clock_2_out));
  Register #(.width(16)) register_2 (
    .D(multiplexer_3_out), .en(decoder_1_out4), .clk(clock_3_out), .Q(register_2_q));  // open: clr
  Clock clock_3 (.out(clock_3_out));
  Register #(.width(16)) register_3 (
    .D(multiplexer_3_out), .en(decoder_1_out6), .clk(clock_4_out), .Q(register_3_q));  // open: clr
  Clock clock_4 (.out(clock_4_out));
  Register #(.width(16)) IR (.D(multiplexer_10_out), .en(fetch), .clk(clock_5_out), .Q(IR_q));  // open: clr
  Clock clock_5 (.out(clock_5_out));
  D_Flip_Flop d_ff_1 (.D(fetch), .clk(clock_6_out), .Q(execute), .Qn(fetch));  // open: preset, reset
  Clock clock_6 (.out(clock_6_out));
  Register #(.width(16)) register_4 (
    .D(multiplexer_3_out), .en(decoder_1_out1), .clk(clock_7_out), .Q(register_4_q));  // open: clr
  Clock clock_7 (.out(clock_7_out));
  Register #(.width(16)) register_5 (
    .D(multiplexer_3_out), .en(decoder_1_out3), .clk(clock_8_out), .Q(register_5_q));  // open: clr
  Clock clock_8 (.out(clock_8_out));
  Register #(.width(16)) register_6 (
    .D(multiplexer_3_out), .en(decoder_1_out5), .clk(clock_9_out), .Q(register_6_q));  // open: clr
  Clock clock_9 (.out(clock_9_out));
  Register #(.width(16)) register_7 (
    .D(multiplexer_3_out), .en(decoder_1_out7), .clk(clock_10_out), .Q(register_7_q));  // open: clr
  Clock clock_10 (.out(clock_10_out));
  Multiplexer #(.width(16)) multiplexer_4 (.in0(IR_q), .in1({16{1'b0}}), .out({multiplexer_4_out, Imm}), .sel(fetch));
  Multiplexer #(.select(3), .width(16)) multiplexer_5 (
    .in0({16{1'b0}}), .in1(register_4_q), .in2(register_1_q), .in3(register_5_q), .in4(register_2_q),
    .in5(register_6_q), .in6(register_3_q), .in7(register_7_q),
    .out({multiplexer_5_out_2[15], multiplexer_5_out}), .sel(Xsel));
  assign bit_extender_2_out = {{15{multiplexer_5_out_2[15]}}, multiplexer_5_out_2[15]};  // Bit_Extender bit_extender_2
  Multiplexer #(.select(3), .width(16)) multiplexer_6 (
    .in0({16{1'b0}}), .in1(register_4_q), .in2(register_1_q), .in3(register_5_q), .in4(register_2_q),
    .in5(register_6_q), .in6(register_3_q), .in7(register_7_q),
    .out({multiplexer_6_out_2, multiplexer_6_out}), .sel(Ysel));
  not not_1 (not_1_out[2], I_R);
  ROM #(.addrWidth(4), .dataWidth(14)) Control_ROM (
    .addr(multiplexer_4_out[15:12]),
    .data({Bltz, Bz, Bnz, Jalr, MemW, MemRx, ImmExt, SrcSel, RegW, I_R, ArithCode}));
  assign Ysel = Imm[2:0] & {3{not_1_out[2]}};  // AND_Gate and_1, 3 bits wide
  Multiplexer #(.width(3)) multiplexer_7 (.in0(Imm[6:4]), .in1(multiplexer_4_out[10:8]), .out(Xsel), .sel(I_R));
  Adder #(.width(16)) adder_3 (
    .a({multiplexer_5_out_2[15], multiplexer_5_out}), .b({multiplexer_6_out_2, multiplexer_6_out}),
    .out(adder_3_out));  // open: cin, cout
  Subtractor #(.width(16)) subtractor_1 (
    .a({multiplexer_5_out_2[15], multiplexer_5_out}), .b({multiplexer_6_out_2, multiplexer_6_out}),
    .out(subtractor_1_out));  // open: bin, bout
  Multiplier #(.mode("twosComplement"), .width(16)) multiplier_1 (
    .a({multiplexer_5_out_2[15], multiplexer_5_out}), .b({multiplexer_6_out_2, multiplexer_6_out}),
    .out(multiplier_1_out));  // open: cin, cout
  Divider #(.mode("twosComplement"), .width(16)) divider_1 (
    .a({multiplexer_5_out_2[15], multiplexer_5_out}), .b({multiplexer_6_out_2, multiplexer_6_out}),
    .out(divider_1_out), .upper(bit_extender_2_out), .rem(divider_1_rem));
  Comparator #(.width(16)) comparator_1 (
    .a({multiplexer_5_out_2[15], multiplexer_5_out}), .b({multiplexer_6_out_2, multiplexer_6_out}),
    .eq(XeqY), .lt(XltY));  // open: gt
  assign and_2_out = {multiplexer_5_out_2[15], multiplexer_5_out} & ~{multiplexer_6_out_2, multiplexer_6_out};  // AND_Gate and_2, 16 bits wide
  assign xor_1_out = {multiplexer_5_out_2[15], multiplexer_5_out} ^ {multiplexer_6_out_2, multiplexer_6_out};  // XOR_Gate xor_1, 16 bits wide
  and and_3 (and_3_out, Bnz, ~XeqY);  // AND_Gate
  and and_4 (and_4_out, Bz, XeqY);
  and and_5 (and_5_out, Bltz, XltY);
  Multiplexer #(.select(3), .width(16)) multiplexer_8 (
    .in0(adder_3_out), .in1(subtractor_1_out), .in2(multiplier_1_out), .in3(divider_1_out), .in4(and_2_out),
    .in5(xor_1_out), .in7(divider_1_rem), .out({multiplexer_8_out, multiplexer_8_out_2}), .sel(ArithCode));  // open: in6
  or or_1 (PCsel[0], and_3_out, and_4_out, and_5_out);
  assign Dsel = multiplexer_4_out[10:8] & {3{RegW}};  // AND_Gate and_6, 3 bits wide
  Multiplexer #(.width(16)) multiplexer_9 (
    .in0({multiplexer_5_out_2[15], multiplexer_5_out}), .in1(PC), .out(multiplexer_9_out), .sel(fetch));
  or or_2 (MemR, MemRx, fetch);
  Comparator #(.width(4)) comparator_2 (
    .a(multiplexer_9_out[15:12]), .b(4'b0000), .eq(comparator_2_eq));  // open: gt, lt
  and and_7 (and_7_out, comparator_2_eq, MemR);
  Comparator #(.width(4)) comparator_3 (
    .a(multiplexer_9_out[15:12]), .b(4'b0010), .eq(comparator_3_eq));  // open: gt, lt
  and and_8 (and_8_out, comparator_3_eq, MemW);
  and and_9 (and_9_out, comparator_3_eq, MemR);
  Comparator #(.width(16)) comparator_4 (.a(multiplexer_9_out), .b(16'h4000), .eq(comparator_4_eq));  // open: gt, lt
  Comparator #(.width(16)) comparator_5 (.a(multiplexer_9_out), .b(16'h4002), .eq(comparator_5_eq));  // open: gt, lt
  Comparator #(.width(16)) comparator_6 (.a(multiplexer_9_out), .b(16'h4001), .eq(comparator_6_eq));  // open: gt, lt
  ROM #(.addrWidth(12), .dataWidth(16)) ROM_1 (.addr(multiplexer_9_out[11:0]), .data(ROM_1_data));
  RAM #(.addrWidth(12), .dataWidth(16), .enables("line")) RAM_1 (
    .addr(multiplexer_9_out[11:0]), .we(and_8_out), .clk(clock_11_out),
    .din({multiplexer_6_out_2, multiplexer_6_out}), .dout(RAM_1_dout));
  Clock clock_11 (.out(clock_11_out));
  and and_10 (and_10_out, comparator_4_eq, MemW);
  Clock clock_12 (.out(clock_12_out));
  and and_11 (and_11_out, comparator_5_eq, MemR);
  and and_12 (and_12_out, comparator_6_eq, MemR);
  TTY TTY_1 (.data(multiplexer_6_out), .clk(clock_12_out), .we(and_10_out));  // open: clr
  Clock clock_13 (.out(clock_13_out));
  Keyboard Keyboard_1 (
    .clk(clock_13_out), .re(and_11_out), .avail(Keyboard_1_avail), .data(Keyboard_1_data));  // open: clr
  assign bit_extender_3_out = {{9{1'b0}}, Keyboard_1_data};  // Bit_Extender bit_extender_3
  assign bit_extender_4_out = {{15{1'b0}}, Keyboard_1_avail};  // Bit_Extender bit_extender_4
  Multiplexer #(.select(3), .width(16)) multiplexer_10 (
    .in0(ROM_1_data), .in1(RAM_1_dout), .in2(bit_extender_3_out), .in3(bit_extender_4_out), .in7({16{1'b0}}),
    .out(multiplexer_10_out), .sel(or_3_out));  // open: in4, in5, in6
  assign or_3_out = ~{3{priority_encoder_1_gs[2]}} | priority_encoder_1_out;  // OR_Gate or_3, 3 bits wide
  Priority_Encoder priority_encoder_1 (
    .in0(and_7_out), .in1(and_9_out), .in2(and_11_out), .in3(and_12_out), .out(priority_encoder_1_out),
    .gs(priority_encoder_1_gs[2]));  // open: in4, in5, in6, in7, en_in, en_out

  // Other names for the same wires on the sheet: PCsel[1] = Jalr

  // Notes on the sheet:
  //   R2
  //   R4
  //   R6
  //   R0
  //   Fetch / Execute FSM
  //   R1
  //   R3
  //   R5
  //   R7
  //   Y
  //   X
  //   Dst
  //   Beag Computer (von Neumann Architecture)
  //   X
  //   X sign-extended
  //   Y
  //   contents of Control_ROM (hex, n*v repeats v):
  //   10 11 12 13 470 200 130 17 58 d8 14 15 0 808 1008 2008
  //   ALU
  //   Branch condition
  //   Instruction decoder
  //   Data In
  //   Address
  //   Data Out
  //   contents of ROM_1 (hex, n*v repeats v):
  //   9100 8140 9205 932a 9401 5013 1224 d2fe e000
  //   Display
  //   Keyboard
endmodule
